# Fritzing sketch Electric_Ride_On_Car (saved by Fritzing 0.9.3b)
breadboards: 1

parts:
  S2 = H-Bridge with L298N
  Part1 = Arduino Uno (Rev3) - ICSP
  M1 = RioRand LM2596
  M2 = DC Motor
  M3 = DC Motor
  J1 = Basic Servo

nets:
  N1: S2.ENA, Part1.D6_PWM
  N2: S2.IN1, Part1.D8
  N3: S2.IN2, Part1.D9_PWM
  N4: S2.IN3, Part1.D10_PWM/SS
  N5: S2.IN4, Part1.D7
  N6: S2.ENB, Part1.D11_PWM/MOSI
  N7: S2.M1-01, M3.pin_2
  N8: S2.M1-02, M3.pin_1
  N9: S2.M2-01, M2.pin_2
  N10: S2.M2-02, M2.pin_1
  N11: S2.ENA-5V, S2.ENB-5V, Part1.5V
  N12: Part1.A2, J1.pulse
  N13: M1.Pin_3, J1.vcc
  N14: M1.Pin_4, J1.gnd

notes:
  L298 Board and Buck Convertor and not exact
  14.4 Voltage from battery, check Github for proper hookup

custom parts:
  H-Bridge with L298N: h-bridge
